// Logisim project ALU.circ as structural Verilog: 3 circuits, main circuit main
module main (
  input  [2:0] in_1,
  input  [3:0] X,
  input  [3:0] Y,
  input  A_S_cola,
  output [3:0] out_5,
  output Bandera_cero
);

  wire simplealu_1_cola_3, simplealu_2_cola_3, simplealu_3_cola_3;

  SimpleALU simplealu_1 (
    .X(X[0]), .Y(Y[0]), .add_sub(A_S_cola), .cola(A_S_cola), .Result(out_5[0]), .Selector(in_1),
    .cola_3(simplealu_1_cola_3));  // open: cola_2, sub_result
  SimpleALU simplealu_2 (
    .X(X[1]), .Y(Y[1]), .add_sub(A_S_cola), .cola(simplealu_1_cola_3), .Result(out_5[1]), .Selector(in_1),
    .cola_3(simplealu_2_cola_3));  // open: cola_2, sub_result
  SimpleALU simplealu_3 (
    .X(X[2]), .Y(Y[2]), .add_sub(A_S_cola), .cola(simplealu_2_cola_3), .Result(out_5[2]), .Selector(in_1),
    .cola_3(simplealu_3_cola_3));  // open: cola_2, sub_result
  SimpleALU simplealu_4 (
    .X(X[3]), .Y(Y[3]), .add_sub(A_S_cola), .cola(simplealu_3_cola_3), .Result(out_5[3]), .Selector(in_1));  // open: cola_2, sub_result, cola_3
  nor nor_1 (Bandera_cero, out_5[0], out_5[1], out_5[2], out_5[3]);

  // Notes on the sheet:
  //   ACTION TABLE
  //   000 AND
  //   001 OR
  //   010 XOR
  //   011 NOR
  //   100 ADD/SUB
endmodule

module simpleAdd (
  input  cola,
  input  X,
  input  Y,
  output result,
  output cola_2
);

  wire and_1_out, and_2_out, or_1_out;

  and and_1 (and_1_out, Y, X);
  or or_1 (or_1_out, X, Y);
  and and_2 (and_2_out, or_1_out, cola);
  ExactlyOne xor_1 (.out(result), .in0(cola), .in1(Y), .in2(X));
  or or_2 (cola_2, and_2_out, and_1_out);
endmodule

module SimpleALU (
  input  X,
  input  [2:0] Selector,
  input  Y,
  input  add_sub,
  input  cola,
  input  cola_2,
  output Result,
  output sub_result,
  output cola_3
);

  wire and_1_out, nor_1_out, or_1_out, xor_1_out, xor_2_out;

  and and_1 (and_1_out, X, Y);
  or or_1 (or_1_out, X, Y);
  xor xor_1 (xor_1_out, X, Y);
  nor nor_1 (nor_1_out, X, Y);
  xor xor_2 (xor_2_out, Y, add_sub);
  simpleAdd simpleadd_1 (.result(sub_result), .cola_2(cola_3), .X(xor_2_out), .Y(X), .cola(cola));
  Multiplexer #(.select(3)) multiplexer_1 (
    .in0(and_1_out), .in1(or_1_out), .in2(xor_1_out), .in3(nor_1_out), .in4(sub_result), .in5(cola_2),
    .out(Result), .sel(Selector));  // open: in6, in7, en

  // Notes on the sheet:
  //   ACTION TABLE
  //   000 AND
  //   001 OR
  //   010 XOR
  //   011 NOR
  //   100 ADD/SUB
endmodule
